# Fritzing sketch arduino_diagramm (saved by Fritzing 0.9.3b)
perfboards: 1

parts:
  DIN1 = DIN-5 jack (MIDI) [package=THT]
  Bauteil1 = Arduino Mega 2560 (Rev3)
  R1 = Resistor [tolerance=±5% resistance=220 package=THT]
  R2 = Resistor [tolerance=±5% resistance=1k package=THT]
  S1 = Pushbutton [package="[THT]"]
  R3 = Rotary Potentiometer (Small) [maximum_resistance=100kΩ package=THT]
  Bauteil2 = Arduino Mega 2560 (Rev3)  # not connected
  J1 = male pin header, 7 pins [form="♂ (male)"]
  R4 = Resistor [tolerance=±5% resistance=1k package=THT]
  R5 = Resistor [tolerance=±5% resistance=1k package=THT]
  R6 = Resistor [tolerance=±5% resistance=1k package=THT]
  R7 = Resistor [tolerance=±5% resistance=1k package=THT]
  R8 = Resistor [tolerance=±5% resistance=1k package=THT]
  R9 = Resistor [tolerance=±5% resistance=1k package=THT]
  J2 = male pin header, 4 pins [form="♂ (male)"]
  R10 = Resistor [tolerance=±5% resistance=220 package=THT]  # not connected
  J3 = male pin header, 7 pins [form="♂ (male)"]  # not connected
  DIN2 = DIN-5 jack (MIDI) [package=THT]  # not connected
  S2 = Pushbutton [package="[THT]"]  # not connected
  S3 = Pushbutton [package="[THT]"]  # not connected
  S4 = Pushbutton [package="[THT]"]  # not connected
  S5 = Pushbutton [package="[THT]"]  # not connected
  S6 = Pushbutton [package="[THT]"]  # not connected

nets:
  N1: DIN1.5, Bauteil1.D1_TX0
  N2: DIN1.2, Bauteil1.GND, R2.Pin_0, R3.leg2
  N3: Bauteil1.A0, R3.wiper
  N4: Bauteil1.5V, R1.Pin_1, R3.leg1
  N5: Bauteil1.D4_PWM, R2.Pin_1, S1.Pin_3, S1.Pin_4
  N6: J1.pin1, R4.Pin_1
  N7: J1.pin2, R5.Pin_1
  N8: J1.pin3, R6.Pin_1
  N9: J1.pin4, R7.Pin_1
  N10: J1.pin5, R8.Pin_1
  N11: J1.pin6, R9.Pin_1
  N12: R4.Pin_0, R5.Pin_0, J2.pin3
